# Fritzing sketch prueba_fritzing (saved by Fritzing 0.9.3b)
breadboards: 1

parts:
  R1 = Resistor [tolerance=±5% resistance=220 package=THT]
  LED1 = LED - 5mm [color="Red (633nm)" package="5 mm [THT]"]
  Componente1 = Arduino Uno (Rev3) - ICSP
  Componente1_2 = Arduino Uno (Rev3) - ICSP

nets:
  N1: R1.Pin_0, LED1.cathode
  GND: R1.Pin_1, Componente1.GND, Componente1_2.GND
  5V: LED1.anode, Componente1.5V, Componente1_2.5V

// code stored in the sketch: Led1.ino

int Led1 = 8;
void setup() {
  pinMode (Led1, OUTPUT);

}

void loop() {
  digitalWrite(Led1, HIGH);
  delay(1000);

}
